# Fritzing sketch remotecontrolFan (saved by Fritzing 0.9.3b)
breadboards: 1

parts:
  Part1 = Elegoo UNO R3 (Rev3)
  M1 = DC Motor
  IC1 = IC, DIP package, 16 pins [chip_label=L293D]
  Part2 = IR Receiver Breakout [package=PCB]
  Part4 = Breadboard Power Supply Board SMD
  VCC1 = Battery block 9V  # not connected

nets:
  N1: Part1.D8, Part2.VCC
  N2: Part1.D3_PWM, IC1.pin7
  N3: Part1.D4, IC1.pin2
  N4: Part1.D5_PWM, IC1.pin1
  N5: Part1.5V, Part2.OUT
  GND: Part1.GND, Part2.GND
  N6: M1.pin_1, M1.pin_2, IC1.pin3, IC1.pin5
  N7: IC1.pin4, Part4.GND
  N8: IC1.pin8, Part4.VCC

custom parts:
  Elegoo UNO R3 (Rev3): The Elegoo R3 is a clone of Arduino Uno, which is a microcontroller board based on the ATmega328 (datasheet). It has 14 digital input/output pins (of which 6 can be used as PWM outputs), 6 analog inputs, a 16 MHz ceramic resonator, a USB connection, a power jack, an ICSP header, and a reset button. It contains everything needed to support the microcontroller; simply connect it to a computer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
