# Fritzing sketch gameController (saved by Fritzing 0.9.3b)
breadboards: 1

parts:
  Part1 = Elegoo UNO R3 (Rev3)
  J1 = Basic Servo
  LED1 = LED - 5mm [color="Red (633nm)" package="5 mm [THT]"]
  LED2 = LED - 5mm [color="Green (560nm)" package="5 mm [THT]"]
  R1 = Resistor [tolerance=±5% resistance=220 package=THT]
  R2 = Resistor [tolerance=±5% resistance=220 package=THT]
  S1 = Pushbutton [package="[THT]"]
  S2 = Pushbutton [package="[THT]"]
  R3 = Resistor [tolerance=±5% resistance=220 package=THT]
  R4 = Resistor [tolerance=±5% resistance=220 package=THT]

nets:
  N1: Part1.D4, S2.Pin_1, S2.Pin_2, R4.Pin_0
  N2: Part1.D5_PWM, S1.Pin_1, S1.Pin_2, R3.Pin_0
  N3: Part1.D6_PWM, R1.Pin_1
  N4: Part1.D7, R2.Pin_1
  5V: Part1.5V, J1.vcc, R3.Pin_1, R4.Pin_1
  GND: Part1.GND, J1.gnd, LED1.cathode, LED2.cathode, S1.Pin_3, S1.Pin_4, S2.Pin_3, S2.Pin_4
  N5: LED1.anode, R2.Pin_0
  N6: LED2.anode, R1.Pin_0

custom parts:
  Elegoo UNO R3 (Rev3): The Elegoo R3 is a clone of Arduino Uno, which is a microcontroller board based on the ATmega328 (datasheet). It has 14 digital input/output pins (of which 6 can be used as PWM outputs), 6 analog inputs, a 16 MHz ceramic resonator, a USB connection, a power jack, an ICSP header, and a reset button. It contains everything needed to support the microcontroller; simply connect it to a computer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
