# Fritzing sketch securitySystem (saved by Fritzing 0.9.3b)
breadboards: 1

parts:
  LED1 = LED - 5mm [color="Green (565nm)" package="5 mm [THT]"]
  R3 = 220Ω Resistor [package=THT]
  Part1 = Elegoo UNO R3 (Rev3)
  J1 = Piezo Speaker
  R6 = 220Ω Resistor [package=THT]
  R8 = 220Ω Resistor [package=THT]
  LED4 = LED - 5mm [color="Yellow (595nm)" package="5 mm [THT]"]
  LED5 = LED - 5mm [color="Red (633nm)" package="5 mm [THT]"]
  R9 = 220Ω Resistor [package=THT]
  hc-sr1 = hc-sr04  # not connected

nets:
  N1: LED1.cathode, Part1.5V, J1.pin1, LED4.cathode, LED5.cathode
  N2: LED1.anode, R3.Pin_0
  N3: R3.Pin_1, Part1.D11_PWM/MOSI
  N4: Part1.D9_PWM, R8.Pin_1
  N5: Part1.D10_PWM/SS, R6.Pin_1
  N6: Part1.D3_PWM, R9.Pin_1
  N7: J1.pin2, R9.Pin_0
  N8: R6.Pin_0, LED4.anode
  N9: R8.Pin_0, LED5.anode

custom parts:
  220Ω Resistor: A generic 5-band resistor (0.25W)
  Elegoo UNO R3 (Rev3): The Elegoo R3 is a clone of Arduino Uno, which is a microcontroller board based on the ATmega328 (datasheet). It has 14 digital input/output pins (of which 6 can be used as PWM outputs), 6 analog inputs, a 16 MHz ceramic resonator, a USB connection, a power jack, an ICSP header, and a reset button. It contains everything needed to support the microcontroller; simply connect it to a computer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
