# Fritzing sketch streetLight (saved by Fritzing 0.9.3b)
breadboards: 1

parts:
  Part1 = Elegoo UNO R3 (Rev3)
  S1 = Momentary Switch [package=ksa_sealed_tac_switch]
  LED7 = LED - 5mm [color="Red (633nm)" package="5 mm [THT]"]
  LED8 = LED - 5mm [color="Yellow (595nm)" package="5 mm [THT]"]
  LED9 = LED - 5mm [color="Green (570nm)" package="5 mm [THT]"]
  R10 = Resistor [tolerance=±1% resistance=10k package=THT]
  R13 = 220Ω Resistor [package=THT]
  R14 = 220Ω Resistor [package=THT]
  R15 = 220Ω Resistor [package=THT]

nets:
  N1: Part1.D8, R15.Pin_1
  N2: Part1.D9_PWM, R14.Pin_1
  N3: Part1.D10_PWM/SS, R13.Pin_1
  N4: Part1.D12/MISO, S1.1
  N5: Part1.5V, S1.4
  N6: Part1.GND, LED7.cathode, LED8.cathode, LED9.cathode, R10.Pin_1
  N7: S1.2, R10.Pin_0
  N8: LED7.anode, R13.Pin_0
  N9: LED8.anode, R14.Pin_0
  N10: LED9.anode, R15.Pin_0

custom parts:
  Elegoo UNO R3 (Rev3): The Elegoo R3 is a clone of Arduino Uno, which is a microcontroller board based on the ATmega328 (datasheet). It has 14 digital input/output pins (of which 6 can be used as PWM outputs), 6 analog inputs, a 16 MHz ceramic resonator, a USB connection, a power jack, an ICSP header, and a reset button. It contains everything needed to support the microcontroller; simply connect it to a computer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
  220Ω Resistor: A generic 5-band resistor (0.25W)
