# Fritzing sketch thermometer (saved by Fritzing 0.9.3b)
breadboards: 1

parts:
  Part1 = Elegoo UNO R3 (Rev3)
  LCD1 = LCD screen
  R1 = 10k Ω Resistor [package=THT]
  R2 = Trimmer Potentiometer [maximum_resistance=10kΩ package=THT]
  R3 = PHOTOCELL [package=photocell-kit]
  R4 = 10k Ω Resistor [package=THT]
  R5 = 10k Ω Resistor [package=THT]
  C1 = Ceramic Capacitor [capacitance=0.1nF voltage=20V package="100 mil [THT, multilayer]"]

nets:
  N1: Part1.A4/SDA, R5.Pin_0, C1.0
  N2: Part1.A5/SCL, R3.P$1, R4.Pin_0
  N3: Part1.D11_PWM/MOSI, LCD1.E
  N4: Part1.D12/MISO, LCD1.RS
  N5: Part1.D2, LCD1.DB7
  N6: Part1.D3_PWM, LCD1.DB6
  N7: Part1.D4, LCD1.DB5
  N8: Part1.D5_PWM, LCD1.DB4
  5V: Part1.5V, LCD1.VDD, R1.Pin_1, R2.leg2, R3.P$2, C1.1
  GND: Part1.GND, LCD1.VSS, LCD1.R/W, LCD1.LED-, R2.leg1, R4.Pin_1, R5.Pin_1
  N9: LCD1.V0, R2.wiper
  N10: LCD1.LED+, R1.Pin_0

custom parts:
  Elegoo UNO R3 (Rev3): The Elegoo R3 is a clone of Arduino Uno, which is a microcontroller board based on the ATmega328 (datasheet). It has 14 digital input/output pins (of which 6 can be used as PWM outputs), 6 analog inputs, a 16 MHz ceramic resonator, a USB connection, a power jack, an ICSP header, and a reset button. It contains everything needed to support the microcontroller; simply connect it to a computer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
  10k Ω Resistor: A generic 5-band resistor (0.25W)
